// Logisim project complementario10.circ as structural Verilog: 1 circuit, main circuit main
module main (
  input  A,
  input  B,
  input  C,
  input  D,
  output Z2,
  output Z1,
  output Z0
);

  wire and_2_out, and_3_out, and_4_out, and_5_out;

  and and_1 (Z2, ~B, ~C, ~D);  // AND_Gate
  and and_2 (and_2_out, B, ~D);  // AND_Gate
  and and_3 (and_3_out, C, ~D);  // AND_Gate
  and and_4 (and_4_out, B, ~C);  // AND_Gate
  and and_5 (and_5_out, ~A, ~C);  // AND_Gate
  or or_1 (Z1, and_2_out, and_3_out);
  or or_2 (Z0, D, and_4_out, and_5_out);
endmodule
