// Logisim project ejercicio4.circ as structural Verilog: 1 circuit, main circuit main
module main (
  input  X,
  input  Y,
  input  Z,
  input  X_2,
  input  Y_2,
  input  Z_2,
  input  A,
  input  B,
  input  C,
  input  D,
  input  A_2,
  input  B_2,
  input  C_2,
  input  D_2,
  output F,
  output F_2,
  output Z_3,
  output Z_4
);

  wire A_C_out, and_1_out, and_2_out, and_3_out, and_4_out, and_5_out, and_6_out, and_7_out, and_9_out,
       and_10_out, B_C_D_out, B_C_out, nor_1_out, or_1_out, or_2_out;

  and and_1 (and_1_out, X, ~Y);  // AND_Gate
  and and_2 (and_2_out, X, Y);
  and and_3 (and_3_out, ~X, Z);  // AND_Gate
  and and_4 (and_4_out, Y, Z);
  and and_5 (and_5_out, B, A);
  and and_6 (and_6_out, D, C);
  nor nor_1 (nor_1_out, and_5_out, and_6_out);
  or or_1 (or_1_out, X, ~Y, and_1_out);  // OR_Gate
  or or_2 (or_2_out, and_2_out, and_3_out, and_4_out);
  and A_C (A_C_out, C, A);
  and B_C_D (B_C_D_out, D, C, B);
  and and_7 (and_7_out, D, A, nor_1_out);
  nand B_C (B_C_out, C, B);
  and and_8 (F, or_1_out, or_2_out);
  or or_3 (Z_3, B_C_out, A_C_out, B_C_D_out, and_7_out);
  or or_4 (Z_4, A_2, ~B_2, ~C_2, D_2);  // OR_Gate
  and and_9 (and_9_out, X_2, Y_2);
  and and_10 (and_10_out, ~X_2, ~Y_2, Z_2);  // AND_Gate
  or or_5 (F_2, and_9_out, and_10_out);
endmodule
