// Logisim project ejercicio5.circ as structural Verilog: 1 circuit, main circuit main
module main (
  input  A,
  input  B,
  input  C,
  input  D,
  input  A_2,
  input  B_2,
  input  C_2,
  input  D_2,
  input  A_3,
  input  B_3,
  input  C_3,
  input  D_3,
  input  A_4,
  input  B_4,
  input  C_4,
  input  D_4,
  input  A_5,
  input  B_5,
  input  C_5,
  input  D_5,
  output out_21,
  output out_22,
  output out_23,
  output out_24,
  output out_25
);

  wire and_1_out, and_2_out, and_3_out, and_4_out, and_5_out, and_6_out, and_7_out, and_8_out, and_10_out,
       and_11_out, and_12_out, and_13_out, and_14_out, and_15_out, and_16_out, and_17_out, and_19_out,
       and_20_out, not_1_out, not_2_out, not_3_out, not_4_out, not_5_out, not_6_out, not_7_out, not_8_out,
       or_1_out, or_2_out, or_3_out, or_4_out, or_5_out, or_6_out, or_8_out, or_9_out, or_10_out, or_11_out,
       or_12_out, or_13_out, or_15_out, or_16_out, xnor_1_out, xnor_2_out;

  not not_1 (not_1_out, D);
  not not_2 (not_2_out, C);
  not not_3 (not_3_out, B);
  not not_4 (not_4_out, A);
  not not_5 (not_5_out, D_4);
  not not_6 (not_6_out, C_4);
  not not_7 (not_7_out, B_4);
  not not_8 (not_8_out, A_4);
  and and_1 (and_1_out, not_4_out, not_2_out, not_1_out);
  and and_2 (and_2_out, not_4_out, not_3_out, not_2_out);
  and and_3 (and_3_out, not_4_out, not_3_out, not_1_out);
  and and_4 (and_4_out, not_3_out, not_2_out, not_1_out);
  and and_5 (and_5_out, A, B, D);
  and and_6 (and_6_out, B, C, D);
  and and_7 (and_7_out, A, C, D);
  and and_8 (and_8_out, A, B, C);
  or or_1 (or_1_out, A_4, B_4, not_6_out, not_5_out);
  or or_2 (or_2_out, A_4, not_7_out, C_4, not_5_out);
  or or_3 (or_3_out, A_4, not_7_out, not_6_out, D_4);
  or or_4 (or_4_out, not_8_out, B_4, C_4, not_5_out);
  or or_5 (or_5_out, not_8_out, B_4, not_6_out, D_4);
  or or_6 (or_6_out, not_8_out, not_7_out, C_4, D_4);
  or or_7 (out_22, and_1_out, and_2_out, and_3_out, and_4_out, and_5_out, and_6_out, and_7_out, and_8_out);
  and and_9 (out_24, or_1_out, or_2_out, or_3_out, or_4_out, or_5_out, or_6_out);
  and and_10 (and_10_out, ~A_2, ~C_2, ~D_2);  // AND_Gate
  and and_11 (and_11_out, ~A_2, ~B_2, ~C_2);  // AND_Gate
  and and_12 (and_12_out, ~A_2, ~B_2, ~D_2);  // AND_Gate
  and and_13 (and_13_out, ~B_2, ~C_2, ~D_2);  // AND_Gate
  and and_14 (and_14_out, A_2, B_2, D_2);
  and and_15 (and_15_out, B_2, C_2, D_2);
  and and_16 (and_16_out, A_2, C_2, D_2);
  and and_17 (and_17_out, A_2, B_2, C_2);
  or or_8 (or_8_out, A_5, B_5, ~C_5, ~D_5);  // OR_Gate
  or or_9 (or_9_out, A_5, ~B_5, C_5, ~D_5);  // OR_Gate
  or or_10 (or_10_out, A_5, ~B_5, ~C_5, D_5);  // OR_Gate
  or or_11 (or_11_out, ~A_5, B_5, C_5, ~D_5);  // OR_Gate
  or or_12 (or_12_out, ~A_5, B_5, ~C_5, D_5);  // OR_Gate
  or or_13 (or_13_out, ~A_5, ~B_5, C_5, D_5);  // OR_Gate
  or or_14 (out_21, and_10_out, and_11_out, and_12_out, and_13_out, and_14_out, and_15_out, and_16_out, and_17_out);
  and and_18 (out_25, or_8_out, or_9_out, or_10_out, or_11_out, or_12_out, or_13_out);
  and and_19 (and_19_out, B_3, A_3);
  or or_15 (or_15_out, C_3, D_3);
  or or_16 (or_16_out, A_3, B_3);
  and and_20 (and_20_out, C_3, D_3);
  xnor xnor_1 (xnor_1_out, and_19_out, or_15_out);
  xnor xnor_2 (xnor_2_out, or_16_out, and_20_out);
  or or_17 (out_23, xnor_1_out, xnor_2_out);
endmodule
