// Logisim project complementario2.circ as structural Verilog: 1 circuit, main circuit main
module main (
  input  A,
  input  B,
  input  C,
  input  D,
  output out_5,
  output out_6,
  output out_7,
  output out_8
);

  wire and_1_out, and_2_out, and_3_out, and_4_out, and_5_out, and_6_out, and_7_out, and_8_out, and_9_out,
       and_10_out, and_11_out, and_12_out;

  and and_1 (and_1_out, A, B, C, D);
  and and_2 (and_2_out, A, ~B, ~C, ~D);  // AND_Gate
  and and_3 (and_3_out, A, ~B, D);  // AND_Gate
  and and_4 (and_4_out, A, ~B, C);  // AND_Gate
  and and_5 (and_5_out, ~A, B, ~C, ~D);  // AND_Gate
  and and_6 (and_6_out, ~A, B, ~C, D);  // AND_Gate
  and and_7 (and_7_out, ~A, B, C, ~D);  // AND_Gate
  and and_8 (and_8_out, A, ~B, ~C, D);  // AND_Gate
  and and_9 (and_9_out, A, ~B, C, ~D);  // AND_Gate
  and and_10 (and_10_out, ~A, B, D);  // AND_Gate
  and and_11 (and_11_out, A, ~B, D);  // AND_Gate
  and and_12 (and_12_out, B, C, D);
  or or_1 (out_5, and_1_out, and_2_out);
  or or_2 (out_6, and_3_out, and_4_out, and_5_out);
  or or_3 (out_7, and_6_out, and_7_out, and_8_out, and_9_out);
  or or_4 (out_8, and_10_out, and_11_out, and_12_out);
endmodule
