// Logisim project complementario4.circ as structural Verilog: 1 circuit, main circuit main
module main (
  input  A1,
  input  A0,
  input  B1,
  input  B0,
  output [3:0] out_5
);

  wire and_2_out, and_3_out, and_4_out, and_5_out, and_6_out, and_7_out;

  and and_1 (out_5[3], A1, A0, B1, B0);
  and and_2 (and_2_out, A1, ~A0, B1);  // AND_Gate
  and and_3 (and_3_out, A1, B1, ~B0);  // AND_Gate
  and and_4 (and_4_out, ~A1, A0, B1);  // AND_Gate
  and and_5 (and_5_out, A1, ~A0, B0);  // AND_Gate
  and and_6 (and_6_out, A1, ~B1, B0);  // AND_Gate
  and and_7 (and_7_out, A0, B1, ~B0);  // AND_Gate
  and and_8 (out_5[0], A0, B0);
  or or_1 (out_5[2], and_2_out, and_3_out);
  or or_2 (out_5[1], and_4_out, and_5_out, and_6_out, and_7_out);
endmodule
