// Logisim project complementario6.circ as structural Verilog: 1 circuit, main circuit main
module main (
  input  _4,
  input  _3,
  input  _2,
  input  _1,
  input  _0,
  output out_6
);

  wire and_1_out, and_2_out, and_3_out, and_4_out, and_5_out, and_6_out, and_7_out, and_8_out, or_1_out,
       or_2_out;

  and and_1 (and_1_out, ~_3, _2, _0);  // AND_Gate
  and and_2 (and_2_out, ~_2, _1, _0);  // AND_Gate
  and and_3 (and_3_out, _2, ~_1, _0);  // AND_Gate
  and and_4 (and_4_out, _3, _2, _0);
  and and_5 (and_5_out, ~_3, ~_2, _0);  // AND_Gate
  and and_6 (and_6_out, _2, _1, _0);
  or or_1 (or_1_out, and_1_out, and_2_out, and_3_out);
  or or_2 (or_2_out, and_4_out, and_5_out, and_6_out);
  and and_7 (and_7_out, or_1_out, ~_4);  // AND_Gate
  and and_8 (and_8_out, _4, or_2_out);
  or or_3 (out_6, and_7_out, and_8_out);
endmodule
