// Logisim project complementario8.circ as structural Verilog: 1 circuit, main circuit main
module main (
  input  A,
  input  B,
  input  C,
  output M1,
  output M2
);

  wire and_1_out, and_2_out, and_3_out, and_4_out;

  and and_1 (and_1_out, ~A, ~B, ~C);  // AND_Gate
  and and_2 (and_2_out, ~A, B, C);  // AND_Gate
  and and_3 (and_3_out, ~A, ~B, ~C);  // AND_Gate
  and and_4 (and_4_out, A, B, ~C);  // AND_Gate
  or or_1 (M1, and_1_out, and_2_out);
  or or_2 (M2, and_3_out, and_4_out);
endmodule
