// Logisim project complementario9.circ as structural Verilog: 1 circuit, main circuit main
module main (
  input  A,
  input  B,
  input  C,
  input  D,
  output out_5
);

  wire nor_1_out, nor_2_out, nor_3_out, nor_4_out;

  nor nor_1 (nor_1_out, A, B, C, ~D);  // NOR_Gate
  nor nor_2 (nor_2_out, A, B, ~C, D);  // NOR_Gate
  nor nor_3 (nor_3_out, A, ~B, C, D);  // NOR_Gate
  nor nor_4 (nor_4_out, ~A, B, C, D);  // NOR_Gate
  or or_1 (out_5, nor_1_out, nor_2_out, nor_3_out, nor_4_out);
endmodule
