// Logisim project ejercicio3.circ as structural Verilog: 1 circuit, main circuit main
module main (
  input  A,
  input  B,
  input  C,
  input  D,
  output F
);

  wire A_C_out, A_D_out, B_C_D_out, minus_A__B__C__D_out, minus_A_C_out;

  and A_D (A_D_out, A, D);
  and B_C_D (B_C_D_out, B, C, D);
  and minus_A_C (minus_A_C_out, ~A, C);  // AND_Gate
  and minus_A__B__C__D (minus_A__B__C__D_out, ~A, ~B, ~C, ~D);  // AND_Gate
  and A_C (A_C_out, A, C);
  or or_1 (F, A_D_out, B_C_D_out, minus_A_C_out, minus_A__B__C__D_out, A_C_out);
endmodule
